# Fritzing sketch Projet_Potager_fritzing (saved by Fritzing 0.9.3b)

parts:
  HC-06 = Bluetooth HC-05 Macho
  Arduino_UNO = Arduino Uno (Rev3)
  Relay_5V = Keyes Relay [package=THT]
  Composant1 = Soil Moisture Sensor

nets:
  N1: HC-06.TXD, Arduino_UNO.D11_PWM/MOSI
  N2: HC-06.RXD, Arduino_UNO.D10_PWM/SS
  VCC: HC-06.VCC, Arduino_UNO.5V, Relay_5V.power, Composant1.VCC
  GND: HC-06.GND, Arduino_UNO.GND, Relay_5V.ground, Composant1.GND
  N3: Arduino_UNO.A0, Composant1.SIG
  N4: Arduino_UNO.D2, Relay_5V.signal
  N5: Relay_5V.NC, Relay_5V.C, Relay_5V.NO

custom parts:
  Keyes Relay: The Keyes 5V relay module is suitable for SCM development, home appliance control. It uses a 5V~12V TIL control signal which can control DC / AC signal.

// code stored in the sketch: bluetoothLight.ino
char blueToothVal;           //value sent over via bluetooth
char lastValue;              //stores last state of device (on/off)
 
void setup()
{
 Serial.begin(9600); 
 pinMode(13,OUTPUT);
 pinMode(12,INPUT);
}
 
 
void loop()
{
  if(Serial.available())
  {//if there is data being recieved
    blueToothVal=Serial.read(); //read it
  }
  if (blueToothVal=='n')
  {//if value from bluetooth serial is n
    digitalWrite(13,HIGH);            //switch on LED
    if (lastValue!='n')
      Serial.println(F("LED is on")); //print LED is on
    lastValue=blueToothVal;
  }
  else if (blueToothVal=='f')
  {//if value from bluetooth serial is n
    digitalWrite(13,LOW);             //turn off LED
    if (lastValue!='f')
      Serial.println(F("LED is off")); //print LED is on
    lastValue=blueToothVal;
  }
  delay(250);
}
